// Logisim project 4-2.circ as structural Verilog: 1 circuit, main circuit main
module main (
  input  X,
  input  Y,
  input  Z,
  input  W,
  output out_5,
  output out_6
);

  wire not_1_out, not_2_out;

  not not_1 (not_1_out, Z);
  not not_2 (not_2_out, W);
  or Out1 (out_5, X, Z);
  and Out2 (out_6, not_1_out, not_2_out);
endmodule
