// Logisim project and.circ as structural Verilog: 1 circuit, main circuit main
module main (
  input  X,
  input  Y,
  output Out
);

  wire nand_1_out;

  nand nand_1 (nand_1_out, X, Y);
  not not_1 (Out, nand_1_out);
endmodule
