// Logisim project myFirst.circ as structural Verilog: 1 circuit, main circuit main
module main (
  input  in_1,
  output out_2
);

  wire nand_1_out, nor_1_out, not_1_out;

  not nand_1 (nand_1_out, in_1);  // NAND_Gate
  not nor_1 (nor_1_out, in_1);  // NOR_Gate
  not not_1 (not_1_out, nor_1_out);
  ExactlyOne xor_1 (.out(out_2), .in0(not_1_out), .in1(not_1_out), .in2(nor_1_out));
endmodule
