// Logisim project or.circ as structural Verilog: 1 circuit, main circuit main
module main (
  input  X,
  input  Y,
  input  X_2,
  input  Y_2,
  output Out,
  output Out_2
);

  wire nand_1_out, nand_2_out, not_1_out, not_2_out;

  not not_1 (not_1_out, X_2);
  not not_2 (not_2_out, Y_2);
  nand nand_1 (nand_1_out, X, X);
  nand nand_2 (nand_2_out, Y, Y);
  nand nand_3 (Out_2, not_1_out, not_2_out);
  nand nand_4 (Out, nand_1_out, nand_2_out);
endmodule
