// Logisim project alu-1.circ as structural Verilog: 3 circuits, main circuit main
module main (
  input  Cin,
  input  [1:0] Operation,
  input  A,
  input  B,
  output Result,
  output Cout
);

  wire and_1_out, n1_bit_adder_1_sum, or_1_out;

  _1_bit_adder u_1_bit_adder_1 (.Cin(Cin), .A(A), .B(B), .Sum(n1_bit_adder_1_sum), .Cout(Cout));
  and and_1 (and_1_out, A, B);
  or or_1 (or_1_out, A, B);
  _4_mux u_4_mux_1 (
    .Selector(Operation), .x0(and_1_out), .x1(or_1_out), .x2(n1_bit_adder_1_sum), .x(Result));  // open: x3
endmodule

module _1_bit_adder (
  input  Cin,
  input  A,
  input  B,
  output Sum,
  output Cout
);

  wire and_1_out, and_2_out, or_1_out;

  or or_1 (or_1_out, A, B);
  and and_1 (and_1_out, A, B);
  or or_2 (Sum, Cin, or_1_out);
  and and_2 (and_2_out, Cin, or_1_out);
  or or_3 (Cout, and_2_out, and_1_out);
endmodule

module _4_mux (
  input  [1:0] Selector,
  input  x0,
  input  x1,
  input  x2,
  input  x3,
  output x
);

  wire and_1_out, and_2_out, and_3_out, and_4_out, not_1_out, not_2_out, not_3_out, not_4_out;

  not not_1 (not_1_out, Selector[0]);
  not not_2 (not_2_out, Selector[1]);
  not not_3 (not_3_out, Selector[1]);
  not not_4 (not_4_out, Selector[0]);
  and and_1 (and_1_out, not_1_out, not_2_out, x0);
  and and_2 (and_2_out, not_3_out, Selector[0], x1);
  and and_3 (and_3_out, not_4_out, Selector[1], x2);
  and and_4 (and_4_out, Selector[1], Selector[0], x3);
  or or_1 (x, and_1_out, and_2_out, and_3_out, and_4_out);
endmodule
