// Logisim project fa-1.circ as structural Verilog: 1 circuit, main circuit main
module main (
  input  Cin,
  input  A,
  input  B,
  output Sum,
  output Cout
);

  wire and_1_out, and_2_out, or_1_out;

  or or_1 (or_1_out, A, B);
  and and_1 (and_1_out, A, B);
  or or_2 (Sum, Cin, or_1_out);
  and and_2 (and_2_out, Cin, or_1_out);
  or or_3 (Cout, and_2_out, and_1_out);
endmodule
