// Logisim project fa-4.circ as structural Verilog: 2 circuits, main circuit main
// +
module main (
  input  Cin,
  input  A0,
  input  B0,
  input  A1,
  input  B1,
  input  A2,
  input  B2,
  input  A3,
  input  B3,
  output Out0,
  output Out1,
  output Out2,
  output Out3,
  output Cout
);

  wire n1_bit_adder_2_cout, n1_bit_adder_3_cout, n1_bit_adder_cout;

  _1_bit_adder u_1_bit_adder (.Cin(Cin), .A(A0), .B(B0), .Sum(Out0), .Cout(n1_bit_adder_cout));
  _1_bit_adder u_1_bit_adder_2 (.Cin(n1_bit_adder_cout), .A(A1), .B(B1), .Sum(Out1), .Cout(n1_bit_adder_2_cout));
  _1_bit_adder u_1_bit_adder_3 (.Cin(n1_bit_adder_2_cout), .A(A2), .B(B2), .Sum(Out2), .Cout(n1_bit_adder_3_cout));
  _1_bit_adder u_1_bit_adder_4 (.Cin(n1_bit_adder_3_cout), .A(A3), .B(B3), .Sum(Out3), .Cout(Cout));
endmodule

module _1_bit_adder (
  input  Cin,
  input  A,
  input  B,
  output Sum,
  output Cout
);

  wire and_1_out, and_2_out, or_1_out;

  or or_1 (or_1_out, A, B);
  and and_1 (and_1_out, A, B);
  or or_2 (Sum, Cin, or_1_out);
  and and_2 (and_2_out, Cin, or_1_out);
  or or_3 (Cout, and_2_out, and_1_out);
endmodule
