// Logisim project mux-2-8.circ as structural Verilog: 1 circuit, main circuit main
module main (
  input  S,
  input  [7:0] in0,
  input  [7:0] in1,
  output [7:0] \output 
);

  wire and_1_out, and_2_out, and_3_out, and_4_out, and_5_out, and_6_out, and_7_out, and_8_out, and_9_out,
       and_10_out, and_11_out, and_12_out, and_13_out, and_14_out, and_15_out, and_16_out, not_1_out;

  not not_1 (not_1_out, S);
  and and_1 (and_1_out, not_1_out, in0[0]);
  and and_2 (and_2_out, not_1_out, in0[1]);
  and and_3 (and_3_out, not_1_out, in0[2]);
  and and_4 (and_4_out, not_1_out, in0[3]);
  and and_5 (and_5_out, not_1_out, in0[4]);
  and and_6 (and_6_out, not_1_out, in0[5]);
  and and_7 (and_7_out, not_1_out, in0[6]);
  and and_8 (and_8_out, not_1_out, in0[7]);
  and and_9 (and_9_out, S, in1[0]);
  and and_10 (and_10_out, S, in1[1]);
  and and_11 (and_11_out, S, in1[2]);
  and and_12 (and_12_out, S, in1[3]);
  and and_13 (and_13_out, S, in1[4]);
  and and_14 (and_14_out, S, in1[5]);
  and and_15 (and_15_out, S, in1[6]);
  and and_16 (and_16_out, S, in1[7]);
  or or_1 (\output [0], and_1_out, and_9_out);
  or or_2 (\output [1], and_2_out, and_10_out);
  or or_3 (\output [2], and_3_out, and_11_out);
  or or_4 (\output [3], and_4_out, and_12_out);
  or or_5 (\output [4], and_5_out, and_13_out);
  or or_6 (\output [5], and_6_out, and_14_out);
  or or_7 (\output [6], and_7_out, and_15_out);
  or or_8 (\output [7], and_8_out, and_16_out);
endmodule
