// Logisim project mux-4i.circ as structural Verilog: 1 circuit, main circuit main
module main (
  input  s0,
  input  s1,
  input  x0,
  input  x1,
  input  x2,
  input  x3,
  output x
);

  wire and_1_out, and_2_out, and_3_out, and_4_out, not_1_out, not_2_out, not_3_out, not_4_out;

  not not_1 (not_1_out, s0);
  not not_2 (not_2_out, s1);
  not not_3 (not_3_out, s1);
  not not_4 (not_4_out, s0);
  and and_1 (and_1_out, not_1_out, not_2_out, x0);
  and and_2 (and_2_out, not_3_out, s0, x1);
  and and_3 (and_3_out, not_4_out, s1, x2);
  and and_4 (and_4_out, s1, s0, x3);
  or or_1 (x, and_1_out, and_2_out, and_3_out, and_4_out);
endmodule
