// Logisim project mux-4ii.circ as structural Verilog: 2 circuits, main circuit main
module _2mux (
  input  S,
  input  x0,
  input  x1,
  output out_4
);

  wire and_1_out, and_2_out, not_1_out;

  not not_1 (not_1_out, S);
  and and_1 (and_1_out, not_1_out, x0);
  and and_2 (and_2_out, S, x1);
  or or_1 (out_4, and_1_out, and_2_out);
endmodule

module main (
  input  s0,
  input  s1,
  input  x0,
  input  x1,
  input  x2,
  input  x3,
  output Out
);

  wire n2mux_1_out_4, n2mux_2_out_4;

  _2mux u_2mux_1 (.S(s0), .x0(x0), .x1(x1), .out_4(n2mux_1_out_4));
  _2mux u_2mux_2 (.S(s0), .x0(x2), .x1(x3), .out_4(n2mux_2_out_4));
  _2mux u_2mux_3 (.S(s1), .x0(n2mux_1_out_4), .x1(n2mux_2_out_4), .out_4(Out));
endmodule
