// Logisim project cla1.circ as structural Verilog: 12 circuits, main circuit cla
module cla (
  input  Cin,
  input  A,
  input  B,
  output S,
  output P,
  output G,
  output Cout
);

  wire and_2_out, and_3_out, and_4_out, and_5_out, and_6_out, and_7_out, and_8_out, not_1_out, not_2_out,
       not_3_out, not_4_out, not_5_out, not_6_out;

  not not_1 (not_1_out, B);
  not not_2 (not_2_out, Cin);
  not not_3 (not_3_out, A);
  not not_4 (not_4_out, Cin);
  not not_5 (not_5_out, A);
  not not_6 (not_6_out, B);
  or or_1 (P, A, B);
  and and_1 (G, A, B);
  and and_2 (and_2_out, A, B);
  and and_3 (and_3_out, A, Cin);
  and and_4 (and_4_out, B, Cin);
  and and_5 (and_5_out, A, B, Cin);
  and and_6 (and_6_out, A, not_1_out, not_2_out);
  and and_7 (and_7_out, not_3_out, B, not_4_out);
  and and_8 (and_8_out, not_5_out, not_6_out, Cin);
  or or_2 (Cout, and_2_out, and_3_out, and_4_out);
  or or_3 (S, and_5_out, and_6_out, and_7_out, and_8_out);
endmodule

module cla1 (
  input  Cin,
  input  A,
  input  B,
  output S,
  output P,
  output G
);

  wire and_1_out, and_2_out, and_3_out, and_4_out, not_1_out, not_2_out, not_3_out, not_4_out, not_5_out,
       not_6_out;

  not not_1 (not_1_out, B);
  not not_2 (not_2_out, Cin);
  not not_3 (not_3_out, A);
  not not_4 (not_4_out, Cin);
  not not_5 (not_5_out, A);
  not not_6 (not_6_out, B);
  and and_1 (and_1_out, A, B, Cin);
  and and_2 (and_2_out, A, not_1_out, not_2_out);
  and and_3 (and_3_out, not_3_out, B, not_4_out);
  and and_4 (and_4_out, not_5_out, not_6_out, Cin);
  or or_1 (P, A, B);
  and and_5 (G, A, B);
  or or_2 (S, and_1_out, and_2_out, and_3_out, and_4_out);
endmodule

module cl_block (
  input  Cin,
  input  G0,
  input  G1,
  input  G2,
  input  P0,
  input  P1,
  input  P2,
  output C1,
  output C2,
  output C3,
  output Gout,
  output Pout
);

  wire and_1_out, and_2_out, and_3_out, and_4_out, and_5_out, and_6_out, and_7_out, and_8_out;

  and and_1 (and_1_out, P0, Cin);
  and and_2 (and_2_out, P1, G0);
  and and_3 (and_3_out, P1, P0, Cin);
  and and_4 (and_4_out, P2, G1);
  and and_5 (and_5_out, P2, P1, G0);
  and and_6 (and_6_out, P2, P1, P0, Cin);
  and and_7 (and_7_out, P2, G1);
  and and_8 (and_8_out, P2, P1, G0);
  and and_9 (Pout, P2, P1, P0);
  or or_1 (C1, G0, and_1_out);
  or or_2 (C2, G1, and_2_out, and_3_out);
  or or_3 (C3, G2, and_4_out, and_5_out, and_6_out);
  or or_4 (Gout, G2, and_7_out, and_8_out);
endmodule

module cl_block_2 (
  input  Cin,
  input  G0,
  input  G1,
  input  G2,
  input  P0,
  input  P1,
  input  P2,
  output C1,
  output C2,
  output C3,
  output Gout,
  output Pout
);

  wire and_1_out, and_2_out, and_3_out, and_4_out, and_5_out;

  and and_1 (and_1_out, P0, Cin);
  and and_2 (and_2_out, P1, G0);
  and and_3 (and_3_out, P1, P0, Cin);
  and and_4 (and_4_out, P2, G1);
  and and_5 (and_5_out, P2, P1, G0);
  and and_6 (Pout, P2, P1, P0);
  or or_1 (C1, G0, and_1_out);
  or or_2 (C2, G1, and_2_out, and_3_out);
  or or_3 (Gout, G2, and_4_out, and_5_out);
endmodule

module cla3 (
  input  Cin,
  input  A0,
  input  B0,
  input  A1,
  input  B1,
  input  A2,
  input  B2,
  output PG,
  output GG,
  output Cout,
  output S0,
  output S1,
  output S2
);

  wire cl_block_1_c1, cl_block_1_c2, cla1_1_g, cla1_1_p, cla1_2_g, cla1_2_p, cla1_3_g, cla1_3_p;

  cla1 cla1_1 (.Cin(Cin), .A(A0), .B(B0), .S(S0), .P(cla1_1_p), .G(cla1_1_g));
  cla1 cla1_2 (.Cin(cl_block_1_c1), .A(A1), .B(B1), .S(S1), .P(cla1_2_p), .G(cla1_2_g));
  cla1 cla1_3 (.Cin(cl_block_1_c2), .A(A2), .B(B2), .S(S2), .P(cla1_3_p), .G(cla1_3_g));
  cl_block_2 cl_block_1 (
    .Cin(Cin), .G0(cla1_1_g), .G1(cla1_2_g), .G2(cla1_3_g), .P0(cla1_1_p), .P1(cla1_2_p), .P2(cla1_3_p),
    .C1(cl_block_1_c1), .C2(cl_block_1_c2), .C3(Cout), .Gout(GG), .Pout(PG));
endmodule

module CLA3 (
  input  Cin,
  input  A0,
  input  B0,
  input  A1,
  input  B1,
  input  A2,
  input  B2,
  output PG,
  output GG,
  output Cout,
  output S0,
  output S1,
  output S2
);

  wire cl_block_1_c1, cl_block_1_c2, cla_1_g, cla_1_p, cla_2_g, cla_2_p, cla_3_g, cla_3_p;

  cla cla_1 (.Cin(Cin), .A(A0), .B(B0), .S(S0), .P(cla_1_p), .G(cla_1_g));  // open: Cout
  cla cla_2 (.Cin(cl_block_1_c1), .A(A1), .B(B1), .S(S1), .P(cla_2_p), .G(cla_2_g));  // open: Cout
  cla cla_3 (.Cin(cl_block_1_c2), .A(A2), .B(B2), .S(S2), .P(cla_3_p), .G(cla_3_g));  // open: Cout
  cl_block cl_block_1 (
    .Cin(Cin), .G0(cla_1_g), .G1(cla_2_g), .G2(cla_3_g), .P0(cla_1_p), .P1(cla_2_p), .P2(cla_3_p),
    .C1(cl_block_1_c1), .C2(cl_block_1_c2), .C3(Cout), .Gout(GG), .Pout(PG));
endmodule

module CLA9 (
  input  Cin,
  input  A0,
  input  B0,
  input  A1,
  input  B1,
  input  A2,
  input  B2,
  input  A3,
  input  B3,
  input  A4,
  input  B4,
  input  A5,
  input  B5,
  input  A6,
  input  B6,
  input  A7,
  input  B7,
  input  A8,
  input  B8,
  output GG,
  output PG,
  output S0,
  output S1,
  output S2,
  output S3,
  output S4,
  output S5,
  output S6,
  output S7,
  output S8
);

  wire cl_block_1_c1, cl_block_1_c2, cla3_1_gg, cla3_1_pg, cla3_2_gg, cla3_2_pg, cla3_3_gg, cla3_3_pg;

  cla3 cla3_1 (
    .Cin(Cin), .A0(A0), .B0(B0), .A1(A1), .B1(B1), .A2(A2), .B2(B2), .PG(cla3_1_pg), .GG(cla3_1_gg), .S0(S0),
    .S1(S1), .S2(S2));  // open: Cout
  cla3 cla3_2 (
    .Cin(cl_block_1_c1), .A0(A3), .B0(B3), .A1(A4), .B1(B4), .A2(A5), .B2(B5), .PG(cla3_2_pg),
    .GG(cla3_2_gg), .S0(S3), .S1(S4), .S2(S5));  // open: Cout
  cla3 cla3_3 (
    .Cin(cl_block_1_c2), .A0(A6), .B0(B6), .A1(A7), .B1(B7), .A2(A8), .B2(B8), .PG(cla3_3_pg),
    .GG(cla3_3_gg), .S0(S6), .S1(S7), .S2(S8));  // open: Cout
  cl_block_2 cl_block_1 (
    .Cin(Cin), .G0(cla3_1_gg), .G1(cla3_2_gg), .G2(cla3_3_gg), .P0(cla3_1_pg), .P1(cla3_2_pg),
    .P2(cla3_3_pg), .C1(cl_block_1_c1), .C2(cl_block_1_c2), .Gout(GG), .Pout(PG));  // open: C3
endmodule

module CLA9_2 (
  input  Cin,
  input  A0,
  input  B0,
  input  A1,
  input  B1,
  input  A2,
  input  B2,
  input  A3,
  input  B3,
  input  A4,
  input  B4,
  input  A5,
  input  B5,
  input  A6,
  input  B6,
  input  A7,
  input  B7,
  input  A8,
  input  B8,
  output GG,
  output PG,
  output S0,
  output S1,
  output S2,
  output S3,
  output S4,
  output S5,
  output S6,
  output S7,
  output S8
);

  wire cl_block_1_c1, cl_block_1_c2, cla3_1_gg, cla3_1_pg, cla3_2_gg, cla3_2_pg, cla3_3_gg, cla3_3_pg;

  CLA3 cla3_1 (
    .Cin(Cin), .A0(A0), .B0(B0), .A1(A1), .B1(B1), .A2(A2), .B2(B2), .PG(cla3_1_pg), .GG(cla3_1_gg), .S0(S0),
    .S1(S1), .S2(S2));  // open: Cout
  CLA3 cla3_2 (
    .Cin(cl_block_1_c1), .A0(A3), .B0(B3), .A1(A4), .B1(B4), .A2(A5), .B2(B5), .PG(cla3_2_pg),
    .GG(cla3_2_gg), .S0(S3), .S1(S4), .S2(S5));  // open: Cout
  CLA3 cla3_3 (
    .Cin(cl_block_1_c2), .A0(A6), .B0(B6), .A1(A7), .B1(B7), .A2(A8), .B2(B8), .PG(cla3_3_pg),
    .GG(cla3_3_gg), .S0(S6), .S1(S7), .S2(S8));  // open: Cout
  cl_block cl_block_1 (
    .Cin(Cin), .G0(cla3_1_gg), .G1(cla3_2_gg), .G2(cla3_3_gg), .P0(cla3_1_pg), .P1(cla3_2_pg),
    .P2(cla3_3_pg), .C1(cl_block_1_c1), .C2(cl_block_1_c2), .Gout(GG), .Pout(PG));  // open: C3
endmodule

module CLA27 (
  input  Cin,
  input  A0,
  input  B0,
  input  A1,
  input  B1,
  input  A2,
  input  B2,
  input  A3,
  input  B3,
  input  A4,
  input  B4,
  input  A5,
  input  B5,
  input  A6,
  input  B6,
  input  A7,
  input  B7,
  input  A8,
  input  B8,
  input  A9,
  input  B9,
  input  A10,
  input  B10,
  input  A11,
  input  B11,
  input  A12,
  input  B12,
  input  A13,
  input  B13,
  input  A14,
  input  B14,
  input  A15,
  input  B15,
  input  A16,
  input  B16,
  input  A17,
  input  B17,
  input  A18,
  input  B18,
  input  A19,
  input  B19,
  input  A20,
  input  B20,
  input  A21,
  input  B21,
  input  A22,
  input  B22,
  input  A23,
  input  B23,
  input  A24,
  input  B24,
  input  A25,
  input  B25,
  input  A26,
  input  B26,
  output S0,
  output S1,
  output S2,
  output S3,
  output S4,
  output S5,
  output S0_2,
  output S7,
  output S8,
  output GG,
  output PG,
  output S9,
  output S10,
  output S11,
  output S12,
  output S13,
  output S14,
  output S15,
  output S16,
  output S17,
  output S18,
  output S19,
  output S20,
  output S21,
  output S22,
  output S23,
  output S24,
  output S25,
  output S26
);

  wire cl_block_1_c1, cl_block_1_c2, cla9_1_gg, cla9_1_pg, cla9_2_gg, cla9_2_pg, cla9_3_gg, cla9_3_pg;

  CLA9 cla9_1 (
    .Cin(Cin), .A0(A0), .B0(B0), .A1(A1), .B1(B1), .A2(A2), .B2(B2), .A3(A3), .B3(B3), .A4(A4), .B4(B4),
    .A5(A5), .B5(B5), .A6(A6), .B6(B6), .A7(A7), .B7(B7), .A8(A8), .B8(B8), .GG(cla9_1_gg), .PG(cla9_1_pg),
    .S0(S0), .S1(S1), .S2(S2), .S3(S3), .S4(S4), .S5(S5), .S6(S0_2), .S7(S7), .S8(S8));
  CLA9 cla9_2 (
    .Cin(cl_block_1_c1), .A0(A9), .B0(B9), .A1(A10), .B1(B10), .A2(A11), .B2(B11), .A3(A12), .B3(B12),
    .A4(A13), .B4(B13), .A5(A14), .B5(B14), .A6(A15), .B6(B15), .A7(A16), .B7(B16), .A8(A17), .B8(B17),
    .GG(cla9_2_gg), .PG(cla9_2_pg), .S0(S9), .S1(S10), .S2(S11), .S3(S12), .S4(S13), .S5(S14), .S6(S15),
    .S7(S16), .S8(S17));
  CLA9 cla9_3 (
    .Cin(cl_block_1_c2), .A0(A18), .B0(B18), .A1(A19), .B1(B19), .A2(A20), .B2(B20), .A3(A21), .B3(B21),
    .A4(A22), .B4(B22), .A5(A23), .B5(B23), .A6(A24), .B6(B24), .A7(A25), .B7(B25), .A8(A26), .B8(B26),
    .GG(cla9_3_gg), .PG(cla9_3_pg), .S0(S18), .S1(S19), .S2(S20), .S3(S21), .S4(S22), .S5(S23), .S6(S24),
    .S7(S25), .S8(S26));
  cl_block_2 cl_block_1 (
    .Cin(Cin), .G0(cla9_1_gg), .G1(cla9_2_gg), .G2(cla9_3_gg), .P0(cla9_1_pg), .P1(cla9_2_pg),
    .P2(cla9_3_pg), .C1(cl_block_1_c1), .C2(cl_block_1_c2), .Gout(GG), .Pout(PG));  // open: C3
endmodule

module CLA27_2 (
  input  Cin,
  input  A0,
  input  B0,
  input  A1,
  input  B1,
  input  A2,
  input  B2,
  input  A3,
  input  B3,
  input  A4,
  input  B4,
  input  A5,
  input  B5,
  input  A6,
  input  B6,
  input  A7,
  input  B7,
  input  A8,
  input  B8,
  input  A9,
  input  B9,
  input  A10,
  input  B10,
  input  A11,
  input  B11,
  input  A12,
  input  B12,
  input  A13,
  input  B13,
  input  A14,
  input  B14,
  input  A15,
  input  B15,
  input  A16,
  input  B16,
  input  A17,
  input  B17,
  input  A18,
  input  B18,
  input  A19,
  input  B19,
  input  A20,
  input  B20,
  input  A21,
  input  B21,
  input  A22,
  input  B22,
  input  A23,
  input  B23,
  input  A24,
  input  B24,
  input  A25,
  input  B25,
  input  A26,
  input  B26,
  output S0,
  output S1,
  output S2,
  output S3,
  output S4,
  output S5,
  output S0_2,
  output S7,
  output S8,
  output GG,
  output PG,
  output S9,
  output S10,
  output S11,
  output S12,
  output S13,
  output S14,
  output S15,
  output S16,
  output S17,
  output S18,
  output S19,
  output S20,
  output S21,
  output S22,
  output S23,
  output S24,
  output S25,
  output S26
);

  wire cl_block_1_c1, cl_block_1_c2, cla9_1_gg, cla9_1_pg, cla9_2_gg, cla9_2_pg, cla9_3_gg, cla9_3_pg;

  CLA9_2 cla9_1 (
    .Cin(Cin), .A0(A0), .B0(B0), .A1(A1), .B1(B1), .A2(A2), .B2(B2), .A3(A3), .B3(B3), .A4(A4), .B4(B4),
    .A5(A5), .B5(B5), .A6(A6), .B6(B6), .A7(A7), .B7(B7), .A8(A8), .B8(B8), .GG(cla9_1_gg), .PG(cla9_1_pg),
    .S0(S0), .S1(S1), .S2(S2), .S3(S3), .S4(S4), .S5(S5), .S6(S0_2), .S7(S7), .S8(S8));
  CLA9_2 cla9_2 (
    .Cin(cl_block_1_c1), .A0(A9), .B0(B9), .A1(A10), .B1(B10), .A2(A11), .B2(B11), .A3(A12), .B3(B12),
    .A4(A13), .B4(B13), .A5(A14), .B5(B14), .A6(A15), .B6(B15), .A7(A16), .B7(B16), .A8(A17), .B8(B17),
    .GG(cla9_2_gg), .PG(cla9_2_pg), .S0(S9), .S1(S10), .S2(S11), .S3(S12), .S4(S13), .S5(S14), .S6(S15),
    .S7(S16), .S8(S17));
  CLA9_2 cla9_3 (
    .Cin(cl_block_1_c2), .A0(A18), .B0(B18), .A1(A19), .B1(B19), .A2(A20), .B2(B20), .A3(A21), .B3(B21),
    .A4(A22), .B4(B22), .A5(A23), .B5(B23), .A6(A24), .B6(B24), .A7(A25), .B7(B25), .A8(A26), .B8(B26),
    .GG(cla9_3_gg), .PG(cla9_3_pg), .S0(S18), .S1(S19), .S2(S20), .S3(S21), .S4(S22), .S5(S23), .S6(S24),
    .S7(S25), .S8(S26));
  cl_block cl_block_1 (
    .Cin(Cin), .G0(cla9_1_gg), .G1(cla9_2_gg), .G2(cla9_3_gg), .P0(cla9_1_pg), .P1(cla9_2_pg),
    .P2(cla9_3_pg), .C1(cl_block_1_c1), .C2(cl_block_1_c2), .Gout(GG), .Pout(PG));  // open: C3
endmodule

module CLA27_2_2 (
  input  Cin,
  input  A0,
  input  B0,
  input  A1,
  input  B1,
  input  A2,
  input  B2,
  input  A3,
  input  B3,
  input  A4,
  input  B4,
  input  A5,
  input  B5,
  input  A6,
  input  B6,
  input  A7,
  input  B7,
  input  A8,
  input  B8,
  input  A9,
  input  B9,
  input  A10,
  input  B10,
  input  A11,
  input  B11,
  input  A12,
  input  B12,
  input  A13,
  input  B13,
  input  A14,
  input  B14,
  input  A15,
  input  B15,
  input  A16,
  input  B16,
  input  A17,
  input  B17,
  input  A18,
  input  B18,
  input  A19,
  input  B19,
  input  A20,
  input  B20,
  input  A21,
  input  B21,
  input  A22,
  input  B22,
  input  A23,
  input  B23,
  input  A24,
  input  B24,
  input  A25,
  input  B25,
  input  A26,
  input  B26,
  output S0,
  output S1,
  output S2,
  output S3,
  output S4,
  output S5,
  output S0_2,
  output S7,
  output S8,
  output Cout,
  output GG,
  output PG,
  output S9,
  output S10,
  output S11,
  output S12,
  output S13,
  output S14,
  output S15,
  output S16,
  output S17,
  output S18,
  output S19,
  output S20,
  output S21,
  output S22,
  output S23,
  output S24,
  output S25,
  output S26
);

  wire cl_block_1_c1, cl_block_1_c2, cla9_1_gg, cla9_1_pg, cla9_2_gg, cla9_2_pg, cla9_3_gg, cla9_3_pg;

  CLA9 cla9_1 (
    .Cin(Cin), .A0(A0), .B0(B0), .A1(A1), .B1(B1), .A2(A2), .B2(B2), .A3(A3), .B3(B3), .A4(A4), .B4(B4),
    .A5(A5), .B5(B5), .A6(A6), .B6(B6), .A7(A7), .B7(B7), .A8(A8), .B8(B8), .GG(cla9_1_gg), .PG(cla9_1_pg),
    .S0(S0), .S1(S1), .S2(S2), .S3(S3), .S4(S4), .S5(S5), .S6(S0_2), .S7(S7), .S8(S8));
  CLA9 cla9_2 (
    .Cin(cl_block_1_c1), .A0(A9), .B0(B9), .A1(A10), .B1(B10), .A2(A11), .B2(B11), .A3(A12), .B3(B12),
    .A4(A13), .B4(B13), .A5(A14), .B5(B14), .A6(A15), .B6(B15), .A7(A16), .B7(B16), .A8(A17), .B8(B17),
    .GG(cla9_2_gg), .PG(cla9_2_pg), .S0(S9), .S1(S10), .S2(S11), .S3(S12), .S4(S13), .S5(S14), .S6(S15),
    .S7(S16), .S8(S17));
  CLA9 cla9_3 (
    .Cin(cl_block_1_c2), .A0(A18), .B0(B18), .A1(A19), .B1(B19), .A2(A20), .B2(B20), .A3(A21), .B3(B21),
    .A4(A22), .B4(B22), .A5(A23), .B5(B23), .A6(A24), .B6(B24), .A7(A25), .B7(B25), .A8(A26), .B8(B26),
    .GG(cla9_3_gg), .PG(cla9_3_pg), .S0(S18), .S1(S19), .S2(S20), .S3(S21), .S4(S22), .S5(S23), .S6(S24),
    .S7(S25), .S8(S26));
  cl_block cl_block_1 (
    .Cin(Cin), .G0(cla9_1_gg), .G1(cla9_2_gg), .G2(cla9_3_gg), .P0(cla9_1_pg), .P1(cla9_2_pg),
    .P2(cla9_3_pg), .C1(cl_block_1_c1), .C2(cl_block_1_c2), .C3(Cout), .Gout(GG), .Pout(PG));
endmodule

module CL_BLOCK_sp (
  input  Cin,
  input  G0,
  input  G1,
  input  G2,
  input  P0,
  input  P1,
  input  P2,
  output C1,
  output C2,
  output C3
);

  wire and_1_out, and_2_out, and_3_out, and_4_out, and_5_out, and_6_out;

  and and_1 (and_1_out, P0, Cin);
  and and_2 (and_2_out, P1, G0);
  and and_3 (and_3_out, P1, P0, Cin);
  and and_4 (and_4_out, P2, G1);
  and and_5 (and_5_out, P2, P1, G0);
  and and_6 (and_6_out, P2, P1, P0, Cin);
  or or_1 (C1, G0, and_1_out);
  or or_2 (C2, G1, and_2_out, and_3_out);
  or or_3 (C3, G2, and_4_out, and_5_out, and_6_out);
endmodule
