// Logisim project 2Flop-2Wide-2Read (pubbox47.cims.nyu.edu's conflicted copy 2011-11-17).circ as structural Verilog: 1 circuit, main circuit main
module main (
  input  ReadReg1,
  input  ReadReg2,
  output [1:0] RegData1,
  output [1:0] RegData2
);

  wire undriven;
  wire [1:0] d_ff_1_q, d_ff_3_q, undriven_2;

  Clock clock ();  // open: out
  D_Flip_Flop d_ff_1 (.Q(d_ff_1_q[0]));  // open: clk, D, Qn, preset, en, reset
  D_Flip_Flop d_ff_2 (.Q(d_ff_1_q[1]));  // open: clk, D, Qn, preset, en, reset
  D_Flip_Flop d_ff_3 (.Q(d_ff_3_q[0]));  // open: clk, D, Qn, preset, en, reset
  D_Flip_Flop d_ff_4 (.clk(undriven), .Q(d_ff_3_q[1]));  // open: D, Qn, preset, en, reset
  Multiplexer #(.select(2), .width(2)) multiplexer_1 (
    .out(RegData1), .sel({ReadReg2, ReadReg1}), .en(ReadReg1));  // open: in0, in1, in2, in3
  Multiplexer #(.select(2), .width(2)) multiplexer_2 (
    .in0(undriven_2), .in1(d_ff_3_q), .out(RegData2), .sel({ReadReg1, ReadReg2}), .en(ReadReg2));  // open: in2, in3
endmodule
