// Logisim project 2Flop-2Wide-2Read-1Write.circ as structural Verilog: 2 circuits, main circuit main
module main (
  input  ReadReg1,
  input  Write,
  input  ReadReg2,
  output [1:0] RegData1,
  output [1:0] RegData2
);

  wire clock_1_out;
  wire [1:0] Register1_out, Register_0_out;

  Clock clock_1 (.out(clock_1_out));
  _2_bit_register Register_0 (.Clock(clock_1_out), .Write(Write), .Out(Register_0_out));  // open: Data
  _2_bit_register Register1 (.Clock(clock_1_out), .Write(Write), .Out(Register1_out));  // open: Data
  Multiplexer #(.width(2), .enable("false")) multiplexer_1 (
    .in0(Register_0_out), .in1(Register1_out), .out(RegData1), .sel(ReadReg1));
  Multiplexer #(.width(2), .enable("false")) multiplexer_2 (
    .in0(Register_0_out), .in1(Register1_out), .out(RegData2), .sel(ReadReg2));
endmodule

module _2_bit_register (
  input  Clock,
  input  Write,
  input  [1:0] Data,
  output [1:0] Out
);

  wire or_1_out;

  or or_1 (or_1_out, Clock, ~Write);  // OR_Gate
  D_Flip_Flop d_ff_1 (.clk(or_1_out), .D(Data[0]), .Q(Out[0]));  // open: Qn, preset, en, reset
  D_Flip_Flop d_ff_2 (.clk(or_1_out), .D(Data[1]), .Q(Out[1]));  // open: Qn, preset, en, reset
endmodule
