// Logisim project 2Flop-2Wide-2Read.circ as structural Verilog: 1 circuit, main circuit main
module main (
  input  ReadReg1,
  input  ReadReg2,
  output [1:0] RegData1,
  output [1:0] RegData2
);

  wire [1:0] d_ff_1_q, d_ff_3_q;

  Clock clock ();  // open: out
  D_Flip_Flop d_ff_1 (.Q(d_ff_1_q[0]));  // open: clk, D, Qn, preset, en, reset
  D_Flip_Flop d_ff_2 (.Q(d_ff_1_q[1]));  // open: clk, D, Qn, preset, en, reset
  D_Flip_Flop d_ff_3 (.Q(d_ff_3_q[0]));  // open: clk, D, Qn, preset, en, reset
  D_Flip_Flop d_ff_4 (.Q(d_ff_3_q[1]));  // open: clk, D, Qn, preset, en, reset
  Multiplexer #(.width(2)) multiplexer_1 (.in0(d_ff_1_q), .in1(d_ff_3_q), .out(RegData1), .sel(ReadReg1));  // open: en
  Multiplexer #(.width(2)) multiplexer_2 (.in0(d_ff_1_q), .in1(d_ff_3_q), .out(RegData2), .sel(ReadReg2));  // open: en
endmodule
