// Logisim project 4Reg-32Wide-2Read-1Write.circ as structural Verilog: 2 circuits, main circuit main
module main (
  input  [1:0] ReadReg1,
  input  Write,
  input  [1:0] WriteReg,
  input  [31:0] WriteData,
  input  [1:0] ReadReg2,
  output [31:0] ReadData1,
  output [31:0] ReadData2
);

  wire and_1_out, and_2_out, and_3_out, and_4_out, clock_out, decoder_1_out0, decoder_1_out1, decoder_1_out2,
       decoder_1_out3;
  wire [31:0] n32bit_register_1_out, n32bit_register_2_out, n32bit_register_3_out, n32bit_register_4_out;

  Clock clock (.out(clock_out));
  Decoder #(.select(2)) decoder_1 (
    .out0(decoder_1_out0), .out1(decoder_1_out1), .out2(decoder_1_out2), .out3(decoder_1_out3), .sel(WriteReg));  // open: en
  and and_1 (and_1_out, Write, decoder_1_out0);
  and and_2 (and_2_out, Write, decoder_1_out1);
  and and_3 (and_3_out, Write, decoder_1_out2);
  and and_4 (and_4_out, Write, decoder_1_out3);
  _32bit_register u_32bit_register_1 (
    .Data(WriteData), .Write(and_1_out), .Clock(clock_out), .Out(n32bit_register_1_out));
  _32bit_register u_32bit_register_2 (
    .Data(WriteData), .Write(and_2_out), .Clock(clock_out), .Out(n32bit_register_2_out));
  _32bit_register u_32bit_register_3 (
    .Data(WriteData), .Write(and_3_out), .Clock(clock_out), .Out(n32bit_register_3_out));
  _32bit_register u_32bit_register_4 (
    .Data(WriteData), .Write(and_4_out), .Clock(clock_out), .Out(n32bit_register_4_out));
  Multiplexer #(.select(2), .width(32)) multiplexer_1 (
    .in0(n32bit_register_1_out), .in1(n32bit_register_2_out), .in2(n32bit_register_3_out),
    .in3(n32bit_register_4_out), .out(ReadData1), .sel(ReadReg1));  // open: en
  Multiplexer #(.select(2), .width(32)) multiplexer_2 (
    .in0(n32bit_register_1_out), .in1(n32bit_register_2_out), .in2(n32bit_register_3_out),
    .in3(n32bit_register_4_out), .out(ReadData2), .sel(ReadReg2));  // open: en
endmodule

module _32bit_register (
  input  [31:0] Data,
  input  Write,
  input  Clock,
  output [31:0] Out
);

  wire or_1_out;

  or or_1 (or_1_out, ~Write, Clock);  // OR_Gate
  Register #(.width(32)) register_1 (.D(Data), .Q(Out), .clk(or_1_out));  // open: en, clr
endmodule
