// Logisim project alu-4bit.circ as structural Verilog: 5 circuits, main circuit main
module main (
  input  Ainvert,
  input  Bnegate,
  input  [1:0] Operation,
  input  [3:0] A,
  input  [3:0] B,
  input  Less,
  output [3:0] Result,
  output Equal_Zero,
  output Overflow,
  output Cout
);

  wire alu_4_1_cout, alu_4_2_cout, alu_4_3_cout, alu_4_4_set, or_1_out;

  ALU_4 alu_4_1 (
    .Cin(Bnegate), .Ainvert(Ainvert), .Binvert(Bnegate), .A(A[0]), .B(B[0]), .Less(alu_4_4_set),
    .Operation(Operation), .Result(Result[0]), .Cout(alu_4_1_cout));  // open: Set, Overflow
  ALU_4 alu_4_2 (
    .Cin(alu_4_1_cout), .Ainvert(Ainvert), .Binvert(Bnegate), .A(A[1]), .B(B[1]), .Less(Less),
    .Operation(Operation), .Result(Result[1]), .Cout(alu_4_2_cout));  // open: Set, Overflow
  ALU_4 alu_4_3 (
    .Cin(alu_4_2_cout), .Ainvert(Ainvert), .Binvert(Bnegate), .A(A[2]), .B(B[2]), .Less(Less),
    .Operation(Operation), .Result(Result[2]), .Cout(alu_4_3_cout));  // open: Set, Overflow
  ALU_4 alu_4_4 (
    .Cin(alu_4_3_cout), .Ainvert(Ainvert), .Binvert(Bnegate), .A(A[3]), .B(B[3]), .Less(Less),
    .Operation(Operation), .Result(Result[3]), .Set(alu_4_4_set), .Overflow(Overflow), .Cout(Cout));
  or or_1 (or_1_out, Result[1], Result[0], Overflow, Result[2]);
  not not_1 (Equal_Zero, or_1_out);
endmodule

module _1_bit_adder (
  input  Cin,
  input  A,
  input  B,
  output Sum,
  output Cout
);

  wire and_1_out, and_2_out, or_1_out;

  or or_1 (or_1_out, A, B);
  and and_1 (and_1_out, A, B);
  or or_2 (Sum, Cin, or_1_out);
  and and_2 (and_2_out, Cin, or_1_out);
  or or_3 (Cout, and_2_out, and_1_out);
endmodule

module _4_mux (
  input  [1:0] Selector,
  input  x0,
  input  x1,
  input  x2,
  input  x3,
  output x
);

  wire and_1_out, and_2_out, and_3_out, and_4_out, not_1_out, not_2_out, not_3_out, not_4_out;

  not not_1 (not_1_out, Selector[0]);
  not not_2 (not_2_out, Selector[1]);
  not not_3 (not_3_out, Selector[1]);
  not not_4 (not_4_out, Selector[0]);
  and and_1 (and_1_out, not_1_out, not_2_out, x0);
  and and_2 (and_2_out, not_3_out, Selector[0], x1);
  and and_3 (and_3_out, not_4_out, Selector[1], x2);
  and and_4 (and_4_out, Selector[1], Selector[0], x3);
  or or_1 (x, and_1_out, and_2_out, and_3_out, and_4_out);
endmodule

// ALU
module ALU_4 (
  input  Cin,
  input  Ainvert,
  input  Binvert,
  input  [1:0] Operation,
  input  A,
  input  B,
  input  Less,
  output Result,
  output Set,
  output Overflow,
  output Cout
);

  wire and_1_out, n1_bit_adder_1_sum, n2_mux_1_x, n2_mux_2_x, not_1_out, not_2_out, or_1_out;

  not not_1 (not_1_out, A);
  _2_mux u_2_mux_1 (.Selector(Ainvert), .x0(A), .x1(not_1_out), .x(n2_mux_1_x));
  not not_2 (not_2_out, B);
  _2_mux u_2_mux_2 (.Selector(Binvert), .x0(B), .x1(not_2_out), .x(n2_mux_2_x));
  and and_1 (and_1_out, n2_mux_1_x, n2_mux_2_x);
  or or_1 (or_1_out, n2_mux_1_x, n2_mux_2_x);
  _1_bit_adder u_1_bit_adder_1 (.Cin(Cin), .A(n2_mux_1_x), .B(n2_mux_2_x), .Sum(n1_bit_adder_1_sum), .Cout(Cout));
  _4_mux u_4_mux_1 (
    .Selector(Operation), .x0(and_1_out), .x1(or_1_out), .x2(n1_bit_adder_1_sum), .x3(Less), .x(Result));
  xor xor_1 (Overflow, Cin, Cout);
  xor xor_2 (Set, n1_bit_adder_1_sum, Overflow);
endmodule

module _2_mux (
  input  Selector,
  input  x0,
  input  x1,
  output x
);

  wire and_1_out, and_2_out, not_1_out;

  not not_1 (not_1_out, Selector);
  and and_1 (and_1_out, not_1_out, x0);
  and and_2 (and_2_out, Selector, x1);
  or or_1 (x, and_1_out, and_2_out);
endmodule
