// Logisim project ALU.circ as structural Verilog: 4 circuits, main circuit ALU-32
module ALU_8 (
  input  Cin,
  input  [2:0] Operation,
  input  Less,
  input  [7:0] A,
  input  [7:0] B,
  output [7:0] Result,
  output Equal_Zero,
  output Overflow,
  output Cout,
  output Set
);

  wire n1_bit_alu_1_cout, n1_bit_alu_2_cout, n1_bit_alu_3_cout, n1_bit_alu_4_cout, n1_bit_alu_5_cout,
       n1_bit_alu_6_cout, n1_bit_alu_7_cout, or_1_out;

  _1_bit_ALU u_1_bit_alu_1 (
    .Cin(Cin), .Operation(Operation), .A(A[0]), .B(B[0]), .Less(Less), .Result(Result[0]),
    .Cout(n1_bit_alu_1_cout));  // open: Set, Overflow
  _1_bit_ALU u_1_bit_alu_2 (
    .Cin(n1_bit_alu_1_cout), .Operation(Operation), .A(A[1]), .B(B[1]), .Less(1'b0), .Result(Result[1]),
    .Cout(n1_bit_alu_2_cout));  // open: Set, Overflow
  _1_bit_ALU u_1_bit_alu_3 (
    .Cin(n1_bit_alu_2_cout), .Operation(Operation), .A(A[2]), .B(B[2]), .Less(1'b0), .Result(Result[2]),
    .Cout(n1_bit_alu_3_cout));  // open: Set, Overflow
  _1_bit_ALU u_1_bit_alu_4 (
    .Cin(n1_bit_alu_3_cout), .Operation(Operation), .A(A[3]), .B(B[3]), .Less(1'b0), .Result(Result[3]),
    .Cout(n1_bit_alu_4_cout));  // open: Set, Overflow
  _1_bit_ALU u_1_bit_alu_5 (
    .Cin(n1_bit_alu_4_cout), .Operation(Operation), .A(A[4]), .B(B[4]), .Less(1'b0), .Result(Result[4]),
    .Cout(n1_bit_alu_5_cout));  // open: Set, Overflow
  _1_bit_ALU u_1_bit_alu_6 (
    .Cin(n1_bit_alu_5_cout), .Operation(Operation), .A(A[5]), .B(B[5]), .Less(1'b0), .Result(Result[5]),
    .Cout(n1_bit_alu_6_cout));  // open: Set, Overflow
  _1_bit_ALU u_1_bit_alu_7 (
    .Cin(n1_bit_alu_6_cout), .Operation(Operation), .A(A[6]), .B(B[6]), .Less(1'b0), .Result(Result[6]),
    .Cout(n1_bit_alu_7_cout));  // open: Set, Overflow
  _1_bit_ALU u_1_bit_alu_8 (
    .Cin(n1_bit_alu_7_cout), .Operation(Operation), .A(A[7]), .B(B[7]), .Less(1'b0), .Result(Result[7]),
    .Set(Set), .Overflow(Overflow), .Cout(Cout));
  or or_1 (or_1_out, Result[1], Result[0], Result[3], Result[2], Result[4], Result[5], Result[6], Overflow);
  not not_1 (Equal_Zero, or_1_out);
endmodule

module _1_bit_adder (
  input  Cin,
  input  A,
  input  B,
  output Sum,
  output Cout
);

  wire and_1_out, and_2_out, xor_1_out;

  xor xor_1 (xor_1_out, A, B);
  and and_1 (and_1_out, A, B);
  xor xor_2 (Sum, Cin, xor_1_out);
  and and_2 (and_2_out, Cin, xor_1_out);
  or or_1 (Cout, and_2_out, and_1_out);
endmodule

// ALU
module _1_bit_ALU (
  input  Cin,
  input  [2:0] Operation,
  input  A,
  input  B,
  input  Less,
  output Result,
  output Set,
  output Overflow,
  output Cout
);

  wire and_1_out, multiplexer_1_out, n1_bit_adder_1_sum, not_1_out, or_1_out;

  not not_1 (not_1_out, B);
  Multiplexer #(.enable("false")) multiplexer_1 (.in0(B), .in1(not_1_out), .out(multiplexer_1_out), .sel(Operation[2]));
  and and_1 (and_1_out, A, multiplexer_1_out);
  or or_1 (or_1_out, A, multiplexer_1_out);
  _1_bit_adder u_1_bit_adder_1 (.Cin(Cin), .A(A), .B(multiplexer_1_out), .Sum(n1_bit_adder_1_sum), .Cout(Cout));
  Multiplexer #(.select(2), .enable("false")) multiplexer_2 (
    .in0(and_1_out), .in1(or_1_out), .in2(n1_bit_adder_1_sum), .in3(Less), .out(Result), .sel(Operation[1:0]));
  xor xor_1 (Overflow, Cin, Cout);
  xor xor_2 (Set, n1_bit_adder_1_sum, Overflow);
endmodule

module ALU_32 (
  input  [2:0] Operation,
  input  [31:0] A,
  input  [31:0] B,
  output [31:0] Result,
  output Equal_Zero,
  output Overflow,
  output CarryOut
);

  wire alu_8_1_cout, alu_8_1_equal_zero, alu_8_2_cout, alu_8_2_equal_zero, alu_8_3_cout, alu_8_3_equal_zero,
       alu_8_4_equal_zero, alu_8_4_set, not_1_out;

  not not_1 (not_1_out, 1'b1);
  ALU_8 alu_8_1 (
    .Cin(Operation[2]), .Less(alu_8_4_set), .A(A[7:0]), .B(B[7:0]), .Operation(Operation),
    .Result(Result[7:0]), .Equal_Zero(alu_8_1_equal_zero), .Cout(alu_8_1_cout));  // open: Overflow, Set
  ALU_8 alu_8_2 (
    .Cin(alu_8_1_cout), .Less(not_1_out), .A(A[15:8]), .B(B[15:8]), .Operation(Operation),
    .Result(Result[15:8]), .Equal_Zero(alu_8_2_equal_zero), .Cout(alu_8_2_cout));  // open: Overflow, Set
  ALU_8 alu_8_3 (
    .Cin(alu_8_2_cout), .Less(not_1_out), .A(A[23:16]), .B(B[23:16]), .Operation(Operation),
    .Result(Result[23:16]), .Equal_Zero(alu_8_3_equal_zero), .Cout(alu_8_3_cout));  // open: Overflow, Set
  ALU_8 alu_8_4 (
    .Cin(alu_8_3_cout), .Less(not_1_out), .A(A[31:24]), .B(B[31:24]), .Operation(Operation),
    .Result(Result[31:24]), .Equal_Zero(alu_8_4_equal_zero), .Overflow(Overflow), .Cout(CarryOut),
    .Set(alu_8_4_set));
  and and_1 (Equal_Zero, alu_8_1_equal_zero, alu_8_2_equal_zero, alu_8_3_equal_zero, alu_8_4_equal_zero);
endmodule
