// Logisim project Data-Memory.circ as structural Verilog: 1 circuit, main circuit Data Memory
module Data_Memory (
  input  MemWrite,
  input  [7:0] Address,
  input  [31:0] Write_Data,
  input  MemWrite_2,
  output [31:0] Read_Data
);

  wire clock_1_out, not_1_out;

  not not_1 (not_1_out, clock_1_out);
  Clock clock_1 (.out(clock_1_out));
  RAM #(.dataWidth(32), .bus("separate")) ram_1 (
    .addr(Address), .din(Write_Data), .data(Read_Data), .str(MemWrite), .clk(not_1_out), .ld(MemWrite_2));  // open: sel, clr
endmodule
