// Logisim project Instruction-Memory.circ as structural Verilog: 1 circuit, main circuit Instruction Memory
module Instruction_Memory (
  input  [4:0] Read_Address,
  output [31:0] Instruction
);

  ROM #(.addrWidth(5), .dataWidth(32)) rom_1 (.addr(Read_Address), .data(Instruction));  // open: sel
endmodule
