// Logisim project Adder-32.circ as structural Verilog: 1 circuit, main circuit Adder-32
module Adder_32 (
  input  [31:0] A,
  input  [31:0] B,
  output [31:0] Result
);

  ALU_32 alu_32_1 (.Operation(3'b010), .A(A), .B(B), .Result(Result));  // open: CarryOut, Equal_Zero, Overflow
endmodule
