// Logisim project Finale.circ as structural Verilog: 1 circuit, main circuit MIPS- the big one
module MIPS__the_big_one (
);

  wire alu_32_1_equal_zero, and_1_out, main_control_1_alusrc, main_control_1_branch, main_control_1_jump,
       main_control_1_memread, main_control_1_memtoreg, main_control_1_memwrite, main_control_1_regdst,
       main_control_1_regwrite;
  wire [1:0] main_control_1_aluop1;
  wire [2:0] alu_control_1_alu_cntl;
  wire [4:0] multiplexer_1_out, pc_1_out;
  wire [7:0] alu_32_1_result;
  wire [31:0] adder_32_1_result, adder_32_2_result, data_memory_1_p5, instruction_memory_1_instruction,
       multiplexer_2_out, multiplexer_3_out, multiplexer_4_out, multiplexer_5_out, registers_1_readdata1,
       registers_1_readdata2, shift_left_1_out_2, shift_left_2_out_2, sign_extend_1_out_2;
  wire [31:5] pc_1_out_2;
  wire [31:8] alu_32_1_result_2;

  PC pc_1 (.In(multiplexer_3_out), .Out({pc_1_out_2, pc_1_out}));
  Adder_32 adder_32_1 (.A({pc_1_out_2, pc_1_out}), .B(32'h4), .Result(adder_32_1_result));
  Instruction_Memory instruction_memory_1 (.Read_Address(pc_1_out), .Instruction(instruction_memory_1_instruction));
  shift_left shift_left_1 (.in_1({{6{1'b0}}, instruction_memory_1_instruction[25:0]}), .out_2(shift_left_1_out_2));
  Main_Control main_control_1 (
    .OP(instruction_memory_1_instruction[31:26]), .Jump(main_control_1_jump),
    .RegWrite(main_control_1_regwrite), .RegDst(main_control_1_regdst), .ALUSrc(main_control_1_alusrc),
    .MemToReg(main_control_1_memtoreg), .MemRead(main_control_1_memread), .MemWrite(main_control_1_memwrite),
    .Branch(main_control_1_branch), .ALUOp1(main_control_1_aluop1));
  Registers registers_1 (
    .ReadReg1(instruction_memory_1_instruction[22:21]), .Write(main_control_1_regwrite),
    .WriteData(multiplexer_5_out), .ReadReg2(instruction_memory_1_instruction[17:16]),
    .WriteReg(multiplexer_1_out[1:0]), .ReadData1(registers_1_readdata1), .ReadData2(registers_1_readdata2));
  Multiplexer #(.width(5), .enable("false")) multiplexer_1 (
    .in0(instruction_memory_1_instruction[20:16]), .in1(instruction_memory_1_instruction[15:11]),
    .out(multiplexer_1_out), .sel(main_control_1_regdst));
  sign_extend sign_extend_1 (.in_1(instruction_memory_1_instruction[15:0]), .out_2(sign_extend_1_out_2));
  Multiplexer #(.width(32), .enable("false")) multiplexer_2 (
    .in0(registers_1_readdata2), .in1(sign_extend_1_out_2), .out(multiplexer_2_out),
    .sel(main_control_1_alusrc));
  ALU_Control alu_control_1 (
    .F(instruction_memory_1_instruction[5:0]), .ALUOp(main_control_1_aluop1),
    .ALU_cntl(alu_control_1_alu_cntl));
  Adder_32 adder_32_2 (.A(adder_32_1_result), .B(shift_left_2_out_2), .Result(adder_32_2_result));
  shift_left shift_left_2 (.in_1(sign_extend_1_out_2), .out_2(shift_left_2_out_2));
  ALU_32 alu_32_1 (
    .Operation(alu_control_1_alu_cntl), .A(registers_1_readdata1), .B(multiplexer_2_out),
    .Result({alu_32_1_result_2, alu_32_1_result}), .Equal_Zero(alu_32_1_equal_zero));  // open: CarryOut, Overflow
  and and_1 (and_1_out, main_control_1_branch, alu_32_1_equal_zero);
  // Data_Memory data_memory_1: pin names not known; wires that end beside it: alu_32_1_result, registers_1_readdata2, main_control_1_memwrite, main_control_1_memread, data_memory_1_p5
  Multiplexer #(.width(32), .enable("false")) multiplexer_3 (
    .in0({adder_32_1_result[31:28], shift_left_1_out_2[27:0]}), .in1(multiplexer_4_out),
    .out(multiplexer_3_out), .sel(main_control_1_jump));
  Multiplexer #(.width(32), .enable("false")) multiplexer_4 (
    .in0(adder_32_1_result), .in1(adder_32_2_result), .out(multiplexer_4_out), .sel(and_1_out));
  Multiplexer #(.width(32), .enable("false")) multiplexer_5 (
    .in0(data_memory_1_p5), .in1({alu_32_1_result_2, alu_32_1_result}), .out(multiplexer_5_out),
    .sel(main_control_1_memtoreg));
endmodule
