// Logisim project MIPS-Proj.circ as structural Verilog: 4 circuits, main circuit Main-Control
module Main_Control (
  input  [5:0] OP,
  output Jump,
  output RegDst,
  output ALUSrc,
  output MemToReg,
  output RegWrite,
  output MemRead,
  output MemWrite,
  output Branch,
  output [1:0] ALUOp1
);

  and and_1 (ALUOp1[1], ~OP[5], ~OP[4], ~OP[3], ~OP[2], ~OP[1], ~OP[0]);  // AND_Gate
  and and_2 (MemRead, OP[5], ~OP[4], ~OP[3], ~OP[2], OP[1], OP[0]);  // AND_Gate
  and and_3 (MemWrite, OP[5], ~OP[4], OP[3], ~OP[2], OP[1], OP[0]);  // AND_Gate
  and and_4 (ALUOp1[0], ~OP[5], ~OP[4], ~OP[3], OP[2], ~OP[1], ~OP[0]);  // AND_Gate
  and and_5 (Jump, ~OP[0], ~OP[1], ~OP[2], ~OP[3], OP[4], ~OP[5]);  // AND_Gate
  or or_1 (ALUSrc, MemRead, MemWrite);
  or or_2 (RegWrite, ALUOp1[1], MemRead);

  assign Branch = ALUOp1[0];
  assign MemToReg = MemRead;
  assign RegDst = ALUOp1[1];
endmodule

module ALU_Control (
  input  [1:0] ALUOp,
  input  [5:0] F,
  output [2:0] ALU_cntl
);

  wire and_1_out, or_1_out;

  or or_1 (or_1_out, F[3], F[0]);
  and and_1 (and_1_out, ALUOp[1], F[1]);
  and and_2 (ALU_cntl[2], ALUOp[1], or_1_out);
  or or_2 (ALU_cntl[0], ALUOp[0], and_1_out);
  or or_3 (ALU_cntl[1], ~ALUOp[1], ~F[2]);  // OR_Gate

  // Notes on the sheet:
  //   B Negate
  //   Op1
  //   Op0
endmodule

module sign_extend (
  input  [15:0] in_1,
  output [31:0] out_2
);


  assign out_2 = {in_1[15], {16{1'b0}}, in_1[14:0]};
endmodule

module shift_left (
  input  [31:0] in_1,
  output [31:0] out_2
);

  Shifter #(.width(32)) shifter_1 (.in(in_1), .\dist (5'b11110), .out(out_2));
endmodule
