// Logisim project PC.circ as structural Verilog: 1 circuit, main circuit PC
module PC (
  input  [31:0] In,
  output [31:0] Out
);

  wire clock_1_out;

  Clock clock_1 (.out(clock_1_out));
  Register #(.width(32), .trigger("falling")) register_1 (.D(In), .Q(Out), .clk(clock_1_out));  // open: en, clr
endmodule
