// Logisim project ram.circ as structural Verilog: 1 circuit, main circuit main
module main (
  input  [1:0] in_1,
  input  [3:0] in_2,
  input  in_3,
  input  in_4,
  output [3:0] out_5
);

  wire clock_1_out, not_1_out;

  not not_1 (not_1_out, clock_1_out);
  Clock clock_1 (.out(clock_1_out));
  RAM #(.addrWidth(2), .dataWidth(4), .bus("separate")) ram_1 (
    .addr(in_1), .din(in_2), .data(out_5), .str(in_4), .clk(not_1_out), .ld(in_3));  // open: sel, clr
endmodule
